# Fritzing sketch ZAD1 (saved by Fritzing 0.9.3b)
breadboards: 1

parts:
  Part1 = Arduino Uno (Rev3)
  R1 = Resistor [tolerance=±5% resistance=220 package="0402 [SMD]"]
  R2 = Resistor [tolerance=±5% resistance=220 package="0402 [SMD]"]
  R3 = Resistor [tolerance=±5% resistance=220 package="0402 [SMD]"]
  R4 = Resistor [tolerance=±5% resistance=220 package="0402 [SMD]"]
  R5 = Resistor [tolerance=±5% resistance=220 package="0402 [SMD]"]
  R6 = Resistor [tolerance=±5% resistance=220 package="0402 [SMD]"]
  LED5 = smd LED [color="Red (633nm)" package="0603 [SMD]"]
  LED6 = smd LED [color="Red (633nm)" package="0603 [SMD]"]
  LED7 = smd LED [color="Red (633nm)" package="0603 [SMD]"]
  LED8 = smd LED [color="Red (633nm)" package="0603 [SMD]"]
  LED9 = smd LED [color="Red (633nm)" package="0603 [SMD]"]
  LED10 = smd LED [color="Red (633nm)" package="0603 [SMD]"]

nets:
  N1: Part1.GND, LED5.cathode, LED6.cathode, LED7.cathode, LED8.cathode, LED9.cathode, LED10.cathode
  N2: Part1.D2, R6.Pin_1
  N3: Part1.D3_PWM, R5.Pin_1
  N4: Part1.D4, R1.Pin_1
  N5: Part1.D5_PWM, R2.Pin_1
  N6: Part1.D6_PWM, R4.Pin_1
  N7: Part1.D7, R3.Pin_1
  N8: R1.Pin_0, LED8.anode
  N9: R2.Pin_0, LED7.anode
  N10: R3.Pin_0, LED5.anode
  N11: R4.Pin_0, LED6.anode
  N12: R5.Pin_0, LED9.anode
  N13: R6.Pin_0, LED10.anode
