# Fritzing sketch Zad5 (saved by Fritzing 0.9.3b)
breadboards: 1

parts:
  Part1 = Arduino Uno (Rev3)
  S1 = Pushbutton [package="[THT]"]
  S2 = Pushbutton [package="[THT]"]
  S3 = Pushbutton [package="[THT]"]
  R1 = Resistor [tolerance=±5% resistance=220 package="2512 [SMD]"]
  R2 = Resistor [tolerance=±5% resistance=220 package="2512 [SMD]"]
  R3 = Resistor [tolerance=±5% resistance=220 package="2512 [SMD]"]
  R4 = Resistor [tolerance=±5% resistance=220 package="2512 [SMD]"]
  R5 = Resistor [tolerance=±5% resistance=220 package="2512 [SMD]"]
  R6 = Resistor [tolerance=±5% resistance=220 package="2512 [SMD]"]
  R7 = Resistor [tolerance=±5% resistance=220 package="2512 [SMD]"]
  LED1 = LED - 5mm [color="Red (633nm)" package="5 mm [THT]"]
  LED2 = LED - 5mm [color="Red (633nm)" package="5 mm [THT]"]
  LED3 = LED - 5mm [color="Red (633nm)" package="5 mm [THT]"]
  LED4 = LED - 5mm [color="Red (633nm)" package="5 mm [THT]"]

nets:
  N1: Part1.D8, R4.Pin_1
  N2: Part1.D9_PWM, R5.Pin_1
  N3: Part1.D10_PWM/SS, R6.Pin_1
  N4: Part1.D11_PWM/MOSI, R7.Pin_1
  N5: Part1.D2, S1.Pin_1, S1.Pin_2
  N6: Part1.D3_PWM, S2.Pin_1, S2.Pin_2
  N7: Part1.D4, S3.Pin_1, S3.Pin_2
  N8: Part1.GND, R1.Pin_0, R2.Pin_0, R3.Pin_0, LED1.cathode, LED2.cathode, LED3.cathode, LED4.cathode
  N9: S1.Pin_3, S1.Pin_4, R1.Pin_1
  N10: S2.Pin_3, S2.Pin_4, R2.Pin_1
  N11: S3.Pin_3, S3.Pin_4, R3.Pin_1
  N12: R4.Pin_0, LED4.anode
  N13: R5.Pin_0, LED3.anode
  N14: R6.Pin_0, LED2.anode
  N15: R7.Pin_0, LED1.anode
